# Fritzing sketch kitchen-light (saved by Fritzing 0.9.1b)
breadboards: 1

parts:
  Часть1 = Arduino Nano (Rev3.0)
  LED1 = LED - 5mm [color="Blue (430nm)" package="5 mm [THT]"]
  LED2 = LED - 5mm [color="White (8000K)" package="5 mm [THT]"]
  R1 = Resistor [tolerance=±5% resistance=220 package=THT]
  R2 = Resistor [tolerance=±5% resistance=220 package=THT]
  TCRT1 = TCRT5000 sensor module [part_number=151608]
  R3 = Resistor [tolerance=±5% resistance=470 package=THT]
  R4 = Resistor [tolerance=±5% resistance=10k package=THT]

nets:
  N1: Часть1.GND, LED1.cathode, LED2.cathode, TCRT1.D-, TCRT1.T-
  N2: Часть1.D2, R1.Pin_0
  N3: Часть1.D5, R2.Pin_0
  N4: Часть1.5V, R3.Pin_1, R4.Pin_1
  N5: Часть1.A0, TCRT1.T+, R4.Pin_0
  N6: LED1.anode, R1.Pin_1
  N7: LED2.anode, R2.Pin_1
  N8: TCRT1.D+, R3.Pin_0

custom parts:
  TCRT5000 sensor module: breakout board with TCRT5000
